# Fritzing sketch Sketch (saved by Fritzing 0.9.5d)
perfboards: 1

parts:
  3_3V_Voltage_Regulator = Voltage Regulator - 3.3V [package="TO220 [THT]"]
  CC1101_8_7 = female pin header, 2 pins [form="♀ (female)"]
  CC1101_3_4 = female pin header, 2 pins [form="♀ (female)"]
  CC1101_6_5 = female pin header, 2 pins [form="♀ (female)"]
  CC1101_2_1 = female pin header, 2 pins [form="♀ (female)"]
  10uF_Decoupling_Capacitor = Ceramic Capacitor [capacitance=10µF package="100 mil [THT, multilayer]"]
  3_6v_Zener_Diode = Zener Diode [breakdown_voltage=3.6V part_number=1N4732A package="300 mil [THT]"]
  100nF_Decoupling_Capacitor = Ceramic Capacitor [capacitance=100nF package="100 mil [THT, multilayer]"]
  LED1 = smd LED [color="White (4500K)" package="0805 [SMD]"]
  68_Ohm_Resistor = Resistor [tolerance=±5% resistance=68 package="2512 [SMD]"]
  10_Pin_R-Header = male pin header, 10 pins [form="♂ (male)"]
  8_Pin_R-Header = male pin header, 8 pins [form="♂ (male)"]

nets:
  N1: 3_3V_Voltage_Regulator.input_voltage, 10_Pin_R-Header.pin1
  N2: 3_3V_Voltage_Regulator.GND, 68_Ohm_Resistor.Pin_1, 10_Pin_R-Header.pin3
  N3: 3_3V_Voltage_Regulator.output_voltage, CC1101_2_1.pin1, 10uF_Decoupling_Capacitor.0, 3_6v_Zener_Diode.cathode, 100nF_Decoupling_Capacitor.0, LED1.anode
  N4: CC1101_8_7.pin2, 8_Pin_R-Header.pin3
  N5: CC1101_3_4.pin1, 8_Pin_R-Header.pin4
  N6: CC1101_3_4.pin2, 8_Pin_R-Header.pin6
  N7: CC1101_6_5.pin1, 8_Pin_R-Header.pin2
  N8: CC1101_6_5.pin2, 8_Pin_R-Header.pin5
  N9: CC1101_2_1.pin2, 10uF_Decoupling_Capacitor.1, 3_6v_Zener_Diode.anode, 100nF_Decoupling_Capacitor.1, 8_Pin_R-Header.pin8
  N10: LED1.cathode, 68_Ohm_Resistor.Pin_0
